# Fritzing sketch hair_whole_system (saved by Fritzing 0.9.3b)
breadboards: 1

parts:
  Arduino_UNO = Arduino Uno (Rev3) - ICSP
  R1 = Resistor [tolerance=±5% resistance=10k package="0402 [SMD]"]
  R2 = Resistor [tolerance=±5% resistance=3.3k package="1206 [SMD]"]
  R3 = Resistor [tolerance=±5% resistance=1M package="1206 [SMD]"]
  C1 = Electrolytic Capacitor [capacitance=100pF package="200 mil [THT, electrolytic]"]
  D1_1n4148 = Diode [package=diode-1n4148]
  L1 = Inductor [inductance=10mH package="0805 [SMD]"]
  C2 = Electrolytic Capacitor [capacitance=10nF package="200 mil [THT, electrolytic]"]
  MUX = 74HC4051 [part_number=CD4051B package=so16]
  Q1_NPN = TRANSISTOR_NPN [package=to-92-ammo]
  Q2_NPN = TRANSISTOR_NPN [package=to-92-ammo]
  Q3_PNP = PNP-Transistor [package="TO92 [THT]"]
  THIS_IS_THE_HAIR = Resistor [tolerance=±5% resistance=220 package="0805 [SMD]"]
  R4 = Resistor [tolerance=±5% resistance=220 package="0805 [SMD]"]
  VCC2 = Battery block 9V
  VCC1 = Battery block 9V
  R5 = Resistor [tolerance=±5% resistance=220 package="0805 [SMD]"]
  R6 = Resistor [tolerance=±5% resistance=100 package="0805 [SMD]"]
  R7 = Temperature Sensor (Thermistor) [thermistor_type=NTC package=THT]
  R8 = Resistor [tolerance=±5% resistance=10k package="0805 [SMD]"]

nets:
  N1: Arduino_UNO.A0, R3.Pin_0, C1.+, D1_1n4148.C
  N2: Arduino_UNO.A1, R7.pin_1, R8.Pin_1
  5V: Arduino_UNO.5V, MUX.VDD, R8.Pin_0
  GND: Arduino_UNO.GND, R2.Pin_1, R3.Pin_1, C1.-, MUX.VEE, MUX.VSS, Q1_NPN.E, VCC2.+, VCC1.-, R5.Pin_1, R7.pin_0
  N3: Arduino_UNO.D9_PWM, R1.Pin_1
  N4: Arduino_UNO.D2, R4.Pin_0, R6.Pin_0
  N5: Arduino_UNO.D4, MUX.C
  N6: Arduino_UNO.D5_PWM, MUX.B
  N7: Arduino_UNO.D6_PWM, MUX.A
  N8: Arduino_UNO.VIN, VCC1.+
  N9: R1.Pin_0, R2.Pin_0, L1.pin_1
  N10: D1_1n4148.A, L1.pin_0, C2.+
  N11: C2.-, MUX.IO
  N12: MUX.IO0, Q1_NPN.C, THIS_IS_THE_HAIR.Pin_0
  N13: Q1_NPN.B, R4.Pin_1
  N14: Q2_NPN.E, R5.Pin_0
  N15: Q2_NPN.B, R6.Pin_1
  N16: Q2_NPN.C, Q3_PNP.B
  N17: Q3_PNP.E, VCC2.-
  N18: Q3_PNP.C, THIS_IS_THE_HAIR.Pin_1
